// Digital circuit 32bFA.dig as structural Verilog
module _32bFA (
  input  [31:0] A_31_0,
  input  [31:0] B_31_0,
  input  Cin,
  output [31:0] S_31_0,
  output [3:0] F_3_0
);

  wire _8bfa_1_cout, _8bfa_2_cout, _8bfa_3_cout, _8bfa_4_cout, flag_1_c, flag_1_n, flag_1_v, flag_1_z;

  _8bFA _8bfa_1 (.A_7_0(A_31_0[7:0]), .B_7_0(B_31_0[7:0]), .Cin(Cin), .S_7_0(S_31_0[7:0]), .Cout(_8bfa_1_cout));
  _8bFA _8bfa_2 (
    .A_7_0(A_31_0[15:8]), .B_7_0(B_31_0[15:8]), .Cin(_8bfa_1_cout), .S_7_0(S_31_0[15:8]), .Cout(_8bfa_2_cout));
  _8bFA _8bfa_3 (
    .A_7_0(A_31_0[23:16]), .B_7_0(B_31_0[23:16]), .Cin(_8bfa_2_cout), .S_7_0(S_31_0[23:16]),
    .Cout(_8bfa_3_cout));
  _8bFA _8bfa_4 (
    .A_7_0(A_31_0[31:24]), .B_7_0(B_31_0[31:24]), .Cin(_8bfa_3_cout), .S_7_0(S_31_0[31:24]),
    .Cout(_8bfa_4_cout));
  Flag flag_1 (
    .S_31_0(S_31_0), .A_31_0(A_31_0), .B_31_0(B_31_0), .Cout(_8bfa_4_cout), .Z(flag_1_z), .N(flag_1_n),
    .V(flag_1_v), .C(flag_1_c));
  BusSplitter #(.Bits(4)) bussplitter_1 (
    .D(F_3_0), .OE(1'b0), .D0(flag_1_z), .D1(flag_1_n), .D2(flag_1_v), .D3(flag_1_c));
endmodule
