// Digital circuit 8bFA.dig as structural Verilog
module _8bFA (
  input  [7:0] A_7_0,
  input  [7:0] B_7_0,
  input  Cin,
  output [7:0] S_7_0,
  output Cout
);

  wire bussplitter_1_d0, bussplitter_1_d1, bussplitter_1_d2, bussplitter_1_d3, bussplitter_1_d4,
       bussplitter_1_d5, bussplitter_1_d6, bussplitter_1_d7, bussplitter_2_d0, bussplitter_2_d1,
       bussplitter_2_d2, bussplitter_2_d3, bussplitter_2_d4, bussplitter_2_d5, bussplitter_2_d6,
       bussplitter_2_d7, FA0_cout, FA0_s, FA1_cout, FA1_s, FA2_cout, FA2_s, FA3_cout, FA3_s, FA4_cout, FA4_s,
       FA5_cout, FA5_s, FA6_cout, FA6_s, FA7_s;

  BusSplitter #(.Bits(8)) bussplitter_1 (
    .D(A_7_0), .OE(1'b1), .D0(bussplitter_1_d0), .D1(bussplitter_1_d1), .D2(bussplitter_1_d2),
    .D3(bussplitter_1_d3), .D4(bussplitter_1_d4), .D5(bussplitter_1_d5), .D6(bussplitter_1_d6),
    .D7(bussplitter_1_d7));
  BusSplitter #(.Bits(8)) bussplitter_2 (
    .D(B_7_0), .OE(1'b1), .D0(bussplitter_2_d0), .D1(bussplitter_2_d1), .D2(bussplitter_2_d2),
    .D3(bussplitter_2_d3), .D4(bussplitter_2_d4), .D5(bussplitter_2_d5), .D6(bussplitter_2_d6),
    .D7(bussplitter_2_d7));
  FA FA0 (.A(bussplitter_1_d0), .B(bussplitter_2_d0), .Cin(Cin), .S(FA0_s), .Cout(FA0_cout));
  FA FA1 (.A(bussplitter_1_d1), .B(bussplitter_2_d1), .Cin(FA0_cout), .S(FA1_s), .Cout(FA1_cout));
  FA FA2 (.A(bussplitter_1_d2), .B(bussplitter_2_d2), .Cin(FA1_cout), .S(FA2_s), .Cout(FA2_cout));
  FA FA3 (.A(bussplitter_1_d3), .B(bussplitter_2_d3), .Cin(FA2_cout), .S(FA3_s), .Cout(FA3_cout));
  FA FA4 (.A(bussplitter_1_d4), .B(bussplitter_2_d4), .Cin(FA3_cout), .S(FA4_s), .Cout(FA4_cout));
  FA FA5 (.A(bussplitter_1_d5), .B(bussplitter_2_d5), .Cin(FA4_cout), .S(FA5_s), .Cout(FA5_cout));
  FA FA6 (.A(bussplitter_1_d6), .B(bussplitter_2_d6), .Cin(FA5_cout), .S(FA6_s), .Cout(FA6_cout));
  FA FA7 (.A(bussplitter_1_d7), .B(bussplitter_2_d7), .Cin(FA6_cout), .S(FA7_s), .Cout(Cout));
  BusSplitter #(.Bits(8)) bussplitter_3 (
    .D(S_7_0), .OE(1'b0), .D0(FA0_s), .D1(FA1_s), .D2(FA2_s), .D3(FA3_s), .D4(FA4_s), .D5(FA5_s), .D6(FA6_s),
    .D7(FA7_s));
endmodule
