// Digital circuit ALU.dig as structural Verilog
module ALU (
  input  [31:0] B_32,
  input  [31:0] A_32,
  input  [3:0] ALUOp_4,
  output [31:0] S_32,
  output Zero
);

  wire and_1_out, multiplexer_2_out;
  wire [3:0] ADD___SUB_f_3_0;
  wire [31:0] ADD___SUB_s_31_0, and_2_out, multiplexer_1_out, not_1_out, or_1_out, SLL_out, SRA_out, SRL_out,
       xor_1_out;
  wire [31:31] SLT_lt, SLTU_lt;

  and and_1 (and_1_out, ALUOp_4[0], ~ALUOp_4[1], ~ALUOp_4[2], ~ALUOp_4[3]);  // And
  assign not_1_out = ~B_32;  // Not not_1, 32 bits wide
  assign and_2_out = A_32 & B_32;  // And and_2, 32 bits wide
  assign or_1_out = A_32 | B_32;  // Or or_1, 32 bits wide
  assign xor_1_out = A_32 ^ B_32;  // XOr xor_1, 32 bits wide
  BarrelShifter #(.Bits(32)) SLL (.in(A_32), .shift({1'b0, B_32[4:0]}), .out(SLL_out));
  BarrelShifter #(.Bits(32), .direction("right")) SRL (.in(A_32), .shift({1'b0, B_32[4:0]}), .out(SRL_out));
  BarrelShifter #(.Bits(32), .barrelShifterMode("arithmetic"), .direction("right")) SRA (
    .in(A_32), .shift({1'b0, B_32[4:0]}), .out(SRA_out));
  Comparator #(.Signed("true"), .Bits(32)) SLT (.a(A_32), .b(B_32), .lt(SLT_lt[31]));  // open: gt, eq
  Comparator #(.Bits(32)) SLTU (.a(A_32), .b(B_32), .lt(SLTU_lt[31]));  // open: gt, eq
  Multiplexer #(.Bits(32)) multiplexer_1 (.sel(and_1_out), .in_0(B_32), .in_1(not_1_out), .out(multiplexer_1_out));
  Multiplexer multiplexer_2 (.sel(and_1_out), .in_0(1'b0), .in_1(1'b1), .out(multiplexer_2_out));
  _32bFA ADD___SUB (
    .A_31_0(A_32), .B_31_0(multiplexer_1_out), .Cin(multiplexer_2_out), .S_31_0(ADD___SUB_s_31_0),
    .F_3_0(ADD___SUB_f_3_0));
  Multiplexer #(.Selector_Bits(4), .Bits(32)) multiplexer_3 (
    .sel(ALUOp_4), .in_0(ADD___SUB_s_31_0), .in_1(ADD___SUB_s_31_0), .in_2(and_2_out), .in_3(or_1_out),
    .in_4(xor_1_out), .in_5(SLL_out), .in_6(SRL_out), .in_7(SRA_out), .in_8({SLT_lt[31], {31{1'b0}}}),
    .in_9({SLTU_lt[31], {31{1'b0}}}), .in_10(A_32), .in_11(B_32), .in_12({32{1'b0}}), .in_13({32{1'b0}}),
    .in_14({32{1'b0}}), .in_15({32{1'b0}}), .out(S_32));
  ZERO zero_1 (.Ip(S_32), .Op(Zero));
endmodule
