// Digital circuit Flag.dig as structural Verilog
module Flag (
  input  [31:0] S_31_0,
  input  [31:0] A_31_0,
  input  [31:0] B_31_0,
  input  Cout,
  output Z,
  output N,
  output V,
  output C
);

  wire and_1_out, and_2_out, bussplitter_1_d0, bussplitter_1_d1, bussplitter_1_d2, bussplitter_1_d3,
       bussplitter_1_d4, bussplitter_1_d5, bussplitter_1_d6, bussplitter_1_d7, bussplitter_1_d8,
       bussplitter_1_d9, bussplitter_1_d10, bussplitter_1_d11, bussplitter_1_d12, bussplitter_1_d13,
       bussplitter_1_d14, bussplitter_1_d15, bussplitter_1_d16, bussplitter_1_d17, bussplitter_1_d18,
       bussplitter_1_d19, bussplitter_1_d20, bussplitter_1_d21, bussplitter_1_d22, bussplitter_1_d23,
       bussplitter_1_d24, bussplitter_1_d25, bussplitter_1_d26, bussplitter_1_d27, bussplitter_1_d28,
       bussplitter_1_d29, bussplitter_1_d30, or_1_out, or_2_out, or_3_out, or_4_out, or_5_out, or_6_out,
       or_7_out, or_8_out, or_9_out, or_10_out, or_12_out;

  BusSplitter #(.Bits(32)) bussplitter_1 (
    .D(S_31_0), .OE(1'b1), .D0(bussplitter_1_d0), .D1(bussplitter_1_d1), .D2(bussplitter_1_d2),
    .D3(bussplitter_1_d3), .D4(bussplitter_1_d4), .D5(bussplitter_1_d5), .D6(bussplitter_1_d6),
    .D7(bussplitter_1_d7), .D8(bussplitter_1_d8), .D9(bussplitter_1_d9), .D10(bussplitter_1_d10),
    .D11(bussplitter_1_d11), .D12(bussplitter_1_d12), .D13(bussplitter_1_d13), .D14(bussplitter_1_d14),
    .D15(bussplitter_1_d15), .D16(bussplitter_1_d16), .D17(bussplitter_1_d17), .D18(bussplitter_1_d18),
    .D19(bussplitter_1_d19), .D20(bussplitter_1_d20), .D21(bussplitter_1_d21), .D22(bussplitter_1_d22),
    .D23(bussplitter_1_d23), .D24(bussplitter_1_d24), .D25(bussplitter_1_d25), .D26(bussplitter_1_d26),
    .D27(bussplitter_1_d27), .D28(bussplitter_1_d28), .D29(bussplitter_1_d29), .D30(bussplitter_1_d30),
    .D31(N));
  or or_1 (or_1_out, bussplitter_1_d1, bussplitter_1_d2, bussplitter_1_d3, bussplitter_1_d4);
  or or_2 (or_2_out, bussplitter_1_d5, bussplitter_1_d6, bussplitter_1_d7, bussplitter_1_d8);
  or or_3 (or_3_out, bussplitter_1_d9, bussplitter_1_d10, bussplitter_1_d11, bussplitter_1_d12);
  and and_1 (and_1_out, ~N, A_31_0[31], B_31_0[31]);  // And
  or or_4 (or_4_out, bussplitter_1_d13, bussplitter_1_d14, bussplitter_1_d15, bussplitter_1_d16);
  or or_5 (or_5_out, bussplitter_1_d17, bussplitter_1_d18, bussplitter_1_d19, bussplitter_1_d20);
  or or_6 (or_6_out, bussplitter_1_d21, bussplitter_1_d22, bussplitter_1_d23, bussplitter_1_d24);
  and and_2 (and_2_out, N, ~A_31_0[31], ~B_31_0[31]);  // And
  or or_7 (or_7_out, bussplitter_1_d25, bussplitter_1_d26, bussplitter_1_d27, bussplitter_1_d28);
  or or_8 (or_8_out, bussplitter_1_d29, bussplitter_1_d30, N, bussplitter_1_d0);
  or or_9 (or_9_out, or_1_out, or_2_out, or_3_out, or_4_out);
  or or_10 (or_10_out, or_5_out, or_6_out, or_7_out, or_8_out);
  or or_11 (V, and_1_out, and_2_out);
  or or_12 (or_12_out, or_9_out, or_10_out);
  not not_1 (Z, or_12_out);

  assign C = Cout;
endmodule
