// Digital circuit ZERO.dig as structural Verilog
module ZERO (
  input  [31:0] Ip,
  output Op
);

  wire or_1_out, or_2_out, or_3_out, or_4_out, or_5_out, or_6_out, or_7_out, or_8_out, or_9_out, or_10_out,
       or_11_out;

  or or_1 (or_1_out, Ip[0], Ip[1], Ip[2], Ip[3]);
  or or_2 (or_2_out, Ip[4], Ip[5], Ip[6], Ip[7]);
  or or_3 (or_3_out, Ip[8], Ip[9], Ip[10], Ip[11]);
  or or_4 (or_4_out, Ip[12], Ip[13], Ip[14], Ip[15]);
  or or_5 (or_5_out, Ip[16], Ip[17], Ip[18], Ip[19]);
  or or_6 (or_6_out, Ip[20], Ip[21], Ip[22], Ip[23]);
  or or_7 (or_7_out, Ip[24], Ip[25], Ip[26], Ip[27]);
  or or_8 (or_8_out, Ip[28], Ip[29], Ip[30], Ip[31]);
  or or_9 (or_9_out, or_1_out, or_2_out, or_3_out, or_4_out);
  or or_10 (or_10_out, or_5_out, or_6_out, or_7_out, or_8_out);
  or or_11 (or_11_out, or_9_out, or_10_out);
  not not_1 (Op, or_11_out);
endmodule
