// Digital circuit ALUcon.dig as structural Verilog
module ALUcon (
  input  [1:0] ALUOp_2,
  input  [2:0] f_3,
  input  [6:0] f_7,
  output [3:0] ALUOp_4
);

  ROM #(.AddrBits(6), .Bits(4)) DECODE (.A({ALUOp_2, f_3, f_7[5]}), .sel(1'b1), .D(ALUOp_4));

  // Notes on the sheet:
  //   contents of DECODE (hex, n*v repeats v):
  //   16*0,1,1,15*0,1,5,5,8,8,9,9,4,4,6,7,3,3,2,2
endmodule
