// Digital circuit CONTROL.dig as structural Verilog
module CONTROL (
  input  [6:0] opcode_7,
  output RegWrite,
  output ALUSrc,
  output MemRead,
  output MemWrite,
  output Branch,
  output [1:0] ALUOp_2,
  output MemtoReg,
  output Jump
);

  wire and_1_out, and_2_out;

  ROM #(.AddrBits(7), .Bits(8)) rom_1 (
    .A(opcode_7), .sel(1'b1), .D({RegWrite, ALUSrc, MemRead, MemWrite, MemtoReg, Branch, ALUOp_2}));
  and and_1 (and_1_out, opcode_7[6], opcode_7[5], ~opcode_7[4]);  // And
  and and_2 (and_2_out, opcode_7[2], opcode_7[1], opcode_7[0]);
  and and_3 (Jump, and_1_out, and_2_out);

  // Notes on the sheet:
  //   contents of rom_1 (hex, n*v repeats v):
  //   0,0,0,e8,15*0,c2,15*0,50,15*0,82,47*0,1
endmodule
