// Digital circuit DATAMEM.dig as structural Verilog
module DATAMEM (
  input  [31:0] S_32,
  input  [31:0] rs2,
  input  MW,
  input  MR,
  input  CLK,
  output [31:0] MO
);

  RAMDualPort #(.AddrBits(8), .Bits(32)) DATA (.A(S_32[9:2]), .Din(rs2), .str(MW), .C(CLK), .ld(MR), .D(MO));
endmodule
