// Digital circuit IMEM.dig as structural Verilog
module IMEM (
  input  [31:0] PC_32,
  output [6:0] opcode_7,
  output [4:0] rd_5,
  output [2:0] funct_3,
  output [4:0] rs1_5,
  output [4:0] rs2_5,
  output [6:0] funct_7,
  output [31:0] I_32
);

  ROM #(.AddrBits(6), .Bits(32)) rom_1 (.A(PC_32[7:2]), .sel(1'b1), .D({funct_7, I_32[24:15], funct_3, I_32[11:0]}));

  assign {I_32[31:25], I_32[14:12]} = {funct_7, funct_3};
  assign opcode_7 = I_32[6:0];
  assign rd_5 = I_32[11:7];
  assign rs1_5 = I_32[19:15];
  assign rs2_5 = I_32[24:20];

  // Notes on the sheet:
  //   contents of rom_1 (hex, n*v repeats v):
  //   293,100313,6283b3,30293,38313,ff5ff06f
endmodule
