// Digital circuit IMMGEN.dig as structural Verilog
module IMMGEN (
  input  [31:0] I_32,
  output [31:0] Imm_32
);

  wire [2:0] DECODE_d;
  wire [31:0] B_type_2_out, I_type_0_out, J_type_out, S_type_1_out;

  ROM #(.AddrBits(7), .Bits(3)) DECODE (.A(I_32[6:0]), .sel(1'b1), .D(DECODE_d));
  BitExtender #(.inputBits(12), .outputBits(32)) I_type_0 (.in(I_32[31:20]), .out(I_type_0_out));
  BitExtender #(.inputBits(12), .outputBits(32)) S_type_1 (.in({I_32[31:25], I_32[11:7]}), .out(S_type_1_out));
  BitExtender #(.inputBits(13), .outputBits(32)) B_type_2 (
    .in({I_32[31], I_32[7], I_32[30:25], I_32[11:8], 1'b0}), .out(B_type_2_out));
  BitExtender #(.inputBits(21), .outputBits(32)) J_type (
    .in({I_32[31], I_32[19:12], I_32[20], I_32[30:21], 1'b0}), .out(J_type_out));
  Multiplexer #(.Selector_Bits(3), .Bits(32)) multiplexer_1 (
    .sel(DECODE_d), .in_0(I_type_0_out), .in_1(S_type_1_out), .in_2(B_type_2_out),
    .in_3({I_32[31:12], {12{1'b0}}}), .in_4(J_type_out), .in_5({32{1'b0}}), .in_6({32{1'b0}}),
    .in_7({32{1'b0}}), .out(Imm_32));

  // Notes on the sheet:
  //   contents of DECODE (hex, n*v repeats v):
  //   35*0,1,0,0,0,3,15*0,3,43*0,2,11*0,4
endmodule
