// Digital circuit PC.dig as structural Verilog
module PC (
  input  [31:0] Ip,
  input  CLK,
  output [31:0] Op
);

  Register #(.Bits(32)) register_1 (.D(Ip), .C(CLK), .en(1'b1), .Q(Op));
endmodule
