// Digital circuit PROCESSOR.dig as structural Verilog
module PROCESSOR (
);

  wire alu_1_zero, and_1_out, CLOCK_out, control_1_alusrc, control_1_branch, control_1_jump,
       control_1_memread, control_1_memtoreg, control_1_memwrite, control_1_regwrite, imem_1_p3, imem_1_p5,
       imem_1_p6, or_1_out;
  wire [1:0] control_1_aluop_2;
  wire [2:0] imem_1_p4;
  wire [3:0] alucon_1_aluop_4;
  wire [6:0] imem_1_p2, imem_1_p7;
  wire [31:0] alu_1_s_32, datamem_1_mo, imem_1_p8, immgen_1_imm_32, multiplexer_1_out, multiplexer_2_out,
       pc_1_op, PC_plus_4_s_31_0, PC_plus_Imm_s_31_0, regfile_1_p1, regfile_1_p7, regfile_1_p8;

  Button CLOCK (.out(CLOCK_out));
  PC pc_1 (.Ip(multiplexer_2_out), .CLK(CLOCK_out), .Op(pc_1_op));
  // IMEM imem_1: pin names not known; wires that end beside it: pc_1_op, imem_1_p2, imem_1_p3, imem_1_p4, imem_1_p5, imem_1_p6, imem_1_p7, imem_1_p8
  _32bFA PC_plus_4 (.A_31_0(pc_1_op), .B_31_0(32'h4), .Cin(1'b0), .S_31_0(PC_plus_4_s_31_0));  // open: F_3_0
  CONTROL control_1 (
    .opcode_7(imem_1_p2), .RegWrite(control_1_regwrite), .ALUSrc(control_1_alusrc),
    .MemRead(control_1_memread), .MemWrite(control_1_memwrite), .Branch(control_1_branch),
    .ALUOp_2(control_1_aluop_2), .MemtoReg(control_1_memtoreg), .Jump(control_1_jump));
  // REGFILE regfile_1: pin names not known; wires that end beside it: regfile_1_p1, control_1_regwrite, imem_1_p3, imem_1_p5, imem_1_p6, CLOCK_out, regfile_1_p7, regfile_1_p8
  IMMGEN immgen_1 (.I_32(imem_1_p8), .Imm_32(immgen_1_imm_32));
  Multiplexer #(.Bits(32)) multiplexer_1 (
    .sel(control_1_alusrc), .in_0(regfile_1_p8), .in_1(immgen_1_imm_32), .out(multiplexer_1_out));
  ALUcon alucon_1 (.ALUOp_2(control_1_aluop_2), .f_3(imem_1_p4), .f_7(imem_1_p7), .ALUOp_4(alucon_1_aluop_4));
  _32bFA PC_plus_Imm (
    .A_31_0(pc_1_op), .B_31_0(immgen_1_imm_32), .Cin(1'b0), .S_31_0(PC_plus_Imm_s_31_0));  // open: F_3_0
  ALU alu_1 (
    .A_32(regfile_1_p7), .B_32(multiplexer_1_out), .ALUOp_4(alucon_1_aluop_4), .Zero(alu_1_zero),
    .S_32(alu_1_s_32));
  and and_1 (and_1_out, control_1_branch, alu_1_zero);
  DATAMEM datamem_1 (
    .S_32(alu_1_s_32), .rs2(regfile_1_p8), .MW(control_1_memwrite), .MR(control_1_memread), .CLK(CLOCK_out),
    .MO(datamem_1_mo));
  Multiplexer #(.Bits(32)) multiplexer_2 (
    .sel(or_1_out), .in_0(PC_plus_4_s_31_0), .in_1(PC_plus_Imm_s_31_0), .out(multiplexer_2_out));
  or or_1 (or_1_out, and_1_out, control_1_jump);
  Multiplexer #(.Bits(32)) multiplexer_3 (
    .sel(control_1_memtoreg), .in_0(alu_1_s_32), .in_1(datamem_1_mo), .out(regfile_1_p1));
endmodule
