// Digital circuit REGFILE.dig as structural Verilog
module REGFILE (
  input  [31:0] rd_data32,
  input  WE,
  input  [4:0] rd_5,
  input  CLK,
  input  [4:0] rs1_5,
  input  [4:0] rs2_5,
  output [31:0] rs1_data32,
  output [31:0] rs2_data32
);

  wire or_1_out, or_2_out;
  wire [31:0] registerfile_1_da, registerfile_1_db;

  or or_1 (or_1_out, rs1_5[4], rs1_5[3], rs1_5[2], rs1_5[1], rs1_5[0]);
  RegisterFile #(.AddrBits(5), .Bits(32)) registerfile_1 (
    .Din(rd_data32), .we(WE), .Rw(rd_5), .C(CLK), .Ra(rs1_5), .Rb(rs2_5), .Da(registerfile_1_da),
    .Db(registerfile_1_db));
  or or_2 (or_2_out, rs2_5[4], rs2_5[3], rs2_5[2], rs2_5[1], rs2_5[0]);
  Multiplexer #(.Bits(32)) multiplexer_1 (
    .sel(or_1_out), .in_0({32{1'b0}}), .in_1(registerfile_1_da), .out(rs1_data32));
  Multiplexer #(.Bits(32)) multiplexer_2 (
    .sel(or_2_out), .in_0({32{1'b0}}), .in_1(registerfile_1_db), .out(rs2_data32));
  // Pins of 1 and 5 bits meet at rs1_5
  // Pins of 1 and 5 bits meet at rs2_5
endmodule
